// Logisim project var 1, 10.circ as structural Verilog: 2 circuits, main circuit scheme 1 - (var.1)
module scheme_1____var_1 (
  input  bit4,
  input  bit3,
  input  bit2,
  input  bit1,
  input  bit0,
  output out_6,
  output bit2_2,
  output bit1_2,
  output bit0_2
);

  wire and_1_out, and_2_out, and_3_out, BCRS_out, DFTV_out, GW_out, HJXZ_out, K_out, LM_out, N_out,
       not_1_out, not_2_out, not_3_out, not_4_out, not_5_out, PQ_out;

  not not_1 (not_1_out, bit4);
  not not_2 (not_2_out, bit3);
  not not_3 (not_3_out, bit2);
  not not_4 (not_4_out, bit1);
  not not_5 (not_5_out, bit0);
  and BCRS (BCRS_out, not_2_out, not_3_out, bit1);
  and DFTV (DFTV_out, not_2_out, bit2, not_5_out);
  and HJXZ (HJXZ_out, bit3, not_3_out, not_5_out);
  and LM (LM_out, not_1_out, bit3, bit2, not_4_out);
  and PQ (PQ_out, bit4, not_2_out, not_3_out, not_4_out);
  and GW (GW_out, not_2_out, bit2, bit1, bit0);
  and K (K_out, not_1_out, bit3, not_3_out, bit1, bit0);
  and N (N_out, not_1_out, bit3, bit2, bit1, not_5_out);
  and and_1 (and_1_out, not_1_out, not_2_out, bit2);
  and and_2 (and_2_out, not_1_out, bit3);
  and and_3 (and_3_out, not_1_out, not_2_out, not_3_out, bit1);
  or or_1 (out_6, BCRS_out, DFTV_out, HJXZ_out, LM_out, PQ_out, GW_out, K_out, N_out);
  or or_2 (bit1_2, and_1_out, and_2_out);
  or or_3 (bit0_2, and_2_out, and_3_out);

  assign bit2_2 = bit4;

  // Notes on the sheet:
  //   введённый номер соответствует согласной
  //   номер наибольшего входа
  //   со значением 1
endmodule

module scheme_2____var__10 (
  input  bit3,
  input  bit2,
  input  bit1,
  input  bit0,
  output bit3_2,
  output bit2_2,
  output bit1_2,
  output bit0_2,
  output out_9
);

  wire _1__3_out, _2__3_out, _4__5_out, _5__7_out, _6__7_out, _8__9_out, _9_out, _10__14_out, _10_out,
       _12__14_out, _13_out, _15_out, not_1_out, not_2_out, not_3_out, not_4_out, xnor_1_out, xnor_2_out;

  not not_1 (not_1_out, bit3);
  not not_2 (not_2_out, bit2);
  not not_3 (not_3_out, bit1);
  not not_4 (not_4_out, bit0);
  and _8__9 (_8__9_out, bit3, not_2_out, not_3_out);
  and _10 (_10_out, bit3, not_2_out, bit1, not_4_out);
  and _4__5 (_4__5_out, not_1_out, bit2, not_3_out);
  and _6__7 (_6__7_out, not_1_out, bit2, bit1);
  and _15 (_15_out, bit3, bit2, bit1, bit0);
  and _2__3 (_2__3_out, not_1_out, not_2_out, bit1);
  and _10__14 (_10__14_out, bit3, bit1, not_4_out);
  and _13 (_13_out, bit3, bit2, not_3_out, bit0);
  and _1__3 (_1__3_out, not_1_out, not_2_out, bit0);
  and _5__7 (_5__7_out, not_1_out, bit2, bit0);
  and _9 (_9_out, bit3, not_2_out, not_3_out, bit0);
  and _12__14 (_12__14_out, bit3, bit2, not_4_out);
  xnor xnor_1 (xnor_1_out, bit3, bit0);
  xnor xnor_2 (xnor_2_out, bit2, bit1);
  or or_1 (bit3_2, _8__9_out, _10_out);
  or or_2 (bit2_2, _4__5_out, _6__7_out, _15_out);
  or or_3 (bit1_2, _6__7_out, _2__3_out, _10__14_out, _13_out);
  or or_4 (bit0_2, _1__3_out, _5__7_out, _9_out, _12__14_out);
  and and_1 (out_9, xnor_1_out, xnor_2_out);

  // Notes on the sheet:
  //   числа от 0 до 15
  //   на входах - двоичная запись
  //   проверяем симметричность введённой двоичной записи
  //   на выходах - двоичная запись
  //   остатка деления числа на 11
  //   1 - палиндром, 0 - в ином случае
endmodule
