// Logisim project lab_4.circ as structural Verilog: 6 circuits, main circuit Асинхронный RS триггер с прямыми входами
module \Асинхронный_RS_триггер_с_прямыми_входами  (
  input  R,
  input  S,
  output Q,
  output nQ
);

  nor nor_1 (Q, R, nQ);
  nor nor_2 (nQ, Q, S);
endmodule

module \Асинхронный_RS_триггер_с_инверсными_входами  (
  input  S,
  input  R,
  output Q,
  output nQ
);

  nand nand_1 (Q, S, nQ);
  nand nand_2 (nQ, Q, R);
endmodule

module \Синхронный_RS_триггер  (
  input  S,
  input  C,
  input  R,
  output Q,
  output nQ
);

  wire nand_1_out, nand_2_out;

  nand nand_1 (nand_1_out, S, C);
  nand nand_2 (nand_2_out, C, R);
  nand nand_3 (Q, nand_1_out, nQ);
  nand nand_4 (nQ, Q, nand_2_out);
endmodule

module \S_триггер  (
  input  S,
  input  R,
  output Q,
  output nQ
);

  wire nand_1_out, nand_2_out;

  nand nand_1 (nand_1_out, S, S);
  nand nand_2 (nand_2_out, nand_1_out, R);
  nand nand_3 (Q, nand_1_out, nQ);
  nand nand_4 (nQ, Q, nand_2_out);
endmodule

module \R_триггер  (
  input  S,
  input  R,
  output Q,
  output nQ
);

  wire nand_1_out, nand_2_out;

  nand nand_1 (nand_1_out, S, nand_2_out);
  nand nand_2 (nand_2_out, R, R);
  nand nand_3 (Q, nand_1_out, nQ);
  nand nand_4 (nQ, Q, nand_2_out);
endmodule

module \E_триггер  (
  input  S,
  input  R,
  output Q,
  output nQ
);

  wire nand_1_out, nand_2_out, nand_3_out, nand_4_out;

  nand nand_1 (nand_1_out, S, S);
  nand nand_2 (nand_2_out, R, R);
  nand nand_3 (nand_3_out, S, nand_2_out);
  nand nand_4 (nand_4_out, nand_1_out, R);
  nand nand_5 (Q, nand_3_out, nQ);
  nand nand_6 (nQ, Q, nand_4_out);
endmodule
