// Logisim project lab_6.circ as structural Verilog: 5 circuits, main circuit Схема сравнения
module \Схема_сравнения  (
  input  x1,
  input  x2,
  output Y
);

  wire \И_2_out , \И_out , \НЕ_2_out , \НЕ_out ;

  not \u_НЕ  (\НЕ_out , x1);
  not \u_НЕ_2  (\НЕ_2_out , x2);
  and \u_И  (\И_out , \НЕ_out , x2);
  and \u_И_2  (\И_2_out , x1, \НЕ_2_out );
  or \u_ИЛИ  (Y, \И_out , \И_2_out );
endmodule

module \Полусумматор  (
  input  X1,
  input  X2,
  output \Старший_разряд ,
  output \Младший_разряд 
);

  \Схема_сравнения  \u_Схема_сравнения  (.x1(X1), .x2(X2), .Y(\Младший_разряд ));
  and \u_И  (\Старший_разряд , X1, X2);
endmodule

// SM
module \Сумматор  (
  input  X1,
  input  X2,
  input  Pi,
  output \Перенос ,
  output \Младший_разряд_суммы 
);

  wire \Полусумматор_2_старший_разряд , \Полусумматор_младший_разряд , \Полусумматор_старший_разряд ;

  \Полусумматор  \u_Полусумматор  (
    .X1(X1), .X2(X2), .\Старший_разряд (\Полусумматор_старший_разряд ),
    .\Младший_разряд (\Полусумматор_младший_разряд ));
  \Полусумматор  \u_Полусумматор_2  (
    .X1(\Полусумматор_младший_разряд ), .X2(Pi), .\Старший_разряд (\Полусумматор_2_старший_разряд ),
    .\Младший_разряд (\Младший_разряд_суммы ));
  or \u_ИЛИ  (\Перенос , \Полусумматор_старший_разряд , \Полусумматор_2_старший_разряд );
endmodule

module \Схема_4_сумматоров  (
  input  X4,
  input  Y4,
  input  X3,
  input  Y3,
  input  X2,
  input  Y2,
  input  X1,
  input  Y1,
  input  P0,
  output S5,
  output S4,
  output S3,
  output S2,
  output S1
);

  wire \P1_перенос , \P2_перенос , \P3_перенос ;

  \Сумматор  P1 (.X1(X1), .X2(Y1), .Pi(P0), .\Перенос (\P1_перенос ), .\Младший_разряд_суммы (S1));
  \Сумматор  P2 (.X1(X2), .X2(Y2), .Pi(\P1_перенос ), .\Перенос (\P2_перенос ), .\Младший_разряд_суммы (S2));
  \Сумматор  P3 (.X1(X3), .X2(Y3), .Pi(\P2_перенос ), .\Перенос (\P3_перенос ), .\Младший_разряд_суммы (S3));
  \Сумматор  P4 (.X1(X4), .X2(Y4), .Pi(\P3_перенос ), .\Перенос (S5), .\Младший_разряд_суммы (S4));
endmodule

module \Теор__раздел  (
  input  A,
  input  B,
  input  A_2,
  input  B_2,
  input  P0,
  output S,
  output P,
  output P_2,
  output S_2
);

  wire and_1_out, and_2_out, and_3_out, and_4_out, and_5_out, not_1_out, or_1_out, \ИЛИ_out , \НЕ_out ;

  or \u_ИЛИ  (\ИЛИ_out , A, B);
  and \u_И  (P, A, B);
  and and_1 (and_1_out, A_2, B_2);
  and and_2 (and_2_out, A_2, P0);
  and and_3 (and_3_out, B_2, P0);
  or or_1 (or_1_out, A_2, P0, B_2);
  and and_4 (and_4_out, A_2, B_2, P0);
  not \u_НЕ  (\НЕ_out , P);
  or or_2 (P_2, and_1_out, and_2_out, and_3_out);
  and \u_И_2  (S, \ИЛИ_out , \НЕ_out );
  not not_1 (not_1_out, P_2);
  and and_5 (and_5_out, not_1_out, or_1_out);
  or or_3 (S_2, and_5_out, and_4_out);

  // Notes on the sheet:
  //   Полусумматор
  //   Сумматор
endmodule
